// Logisim project PROJET - DYMKO - MANUEL.circ as structural Verilog: 4 circuits, main circuit unité de calcul PARTIE 1
// Unité de calcul
module \unité_de_calcul_PARTIE_1  (
  input  [7:0] in_1,
  input  [7:0] in_2,
  input  [7:0] in_3,
  output [7:0] out_4,
  output out_5
);

  wire comparator_1_eq, Radd, Rdiv1, Rmul1, Rsou, stop;
  wire [1:0] op;
  wire [7:0] add, div, mul, Rdiv, Rmul, sou, subtractor_1_out;

  Comparator comparator_1 (.a(in_3), .b({8{1'b0}}), .eq(comparator_1_eq));  // open: gt, lt
  not not_1 (stop, comparator_1_eq);
  Subtractor subtractor_1 (.a(in_3), .b(8'h1), .out(subtractor_1_out));  // open: bin, bout
  or or_1 (Rmul1, Rmul[0], Rmul[1], Rmul[2], Rmul[3], Rmul[4], Rmul[5], Rmul[6], Rmul[7]);
  or or_2 (Rdiv1, Rdiv[0], Rdiv[1], Rdiv[2], Rdiv[3], Rdiv[4], Rdiv[5], Rdiv[6], Rdiv[7]);
  Adder adder_1 (.a(in_1), .b(in_2), .out(add), .cout(Radd));  // open: cin
  assign op = stop ? subtractor_1_out[1:0] : 2'bz;  // Controlled_Buffer controlled_buffer_1
  Multiplier multiplier_1 (.a(in_1), .b(in_2), .out(mul), .cout(Rmul));  // open: cin
  Soustracteur_en_valeur_absolut soustracteur_en_valeur_absolut_1 (.in_1(in_1), .in_2(in_2), .out_3(sou), .out_4(Rsou));
  Divider divider_1 (.a(in_1), .b(in_2), .out(div), .rem(Rdiv));  // open: upper
  Multiplexer #(.select(2), .width(8)) multiplexer_1 (
    .in0(add), .in1(sou), .in2(mul), .in3(div), .out(out_4), .sel(op));  // open: en
  Multiplexer #(.select(2)) multiplexer_2 (
    .in0(Radd), .in1(Rsou), .in2(Rmul1), .in3(Rdiv1), .out(out_5), .sel(op));  // open: en

  // Other names for the same wires on the sheet: nb1[7:0] = in_1; nb2[7:0] = in_2
endmodule

// Soustracteur
module Soustracteur_en_valeur_absolut (
  input  [7:0] in_1,
  input  [7:0] in_2,
  output [7:0] out_3,
  output out_4
);

  wire [7:0] subtractor_1_out, subtractor_2_out;

  Comparator comparator_1 (.a(in_1), .b(in_2), .lt(out_4));  // open: gt, eq
  Subtractor subtractor_1 (.a(in_2), .b(in_1), .out(subtractor_1_out));  // open: bin, bout
  Subtractor subtractor_2 (.a(in_1), .b(in_2), .out(subtractor_2_out));  // open: bin, bout
  Multiplexer #(.width(8)) multiplexer_1 (
    .in0(subtractor_2_out), .in1(subtractor_1_out), .out(out_3), .sel(out_4));  // open: en
endmodule

module \unité_de_calcul_PARTIE_2  (
);

  wire _0_t, _3, and_1_out, and_3_out, clk, clock_1_out, clr, comparator_1_eq, comparator_1_gt,
       comparator_3_eq, comparator_4_eq, imp, retenu, stop, \unité_de_calcul_partie_1_1_out_5 , X, Y;
  wire [7:0] controlled_buffer_2_out, controlled_buffer_3_out, controlled_buffer_4_out, counter_1_q,
       divider_1_rem, multiplexer_1_out, register_1_q, register_2_q, register_3_q, res, rom_1_data;

  Clock clock_1 (.out(clock_1_out));
  or or_1 (_3, comparator_1_eq, comparator_1_gt);
  Counter counter_1 (.Q(counter_1_q), .clk(clk), .clr(clr));  // open: load, D, count, carry
  assign clk = stop ? clock_1_out : 1'bz;  // Controlled_Buffer controlled_buffer_1
  Comparator comparator_1 (.a(counter_1_q), .b(8'h3), .gt(comparator_1_gt), .eq(comparator_1_eq));  // open: lt
  Comparator comparator_2 (.a(counter_1_q), .b({8{1'b0}}), .gt(_0_t), .eq(X));  // open: lt
  Divider divider_1 (.a(counter_1_q), .b(8'h2), .rem(divider_1_rem));  // open: out, upper
  Comparator comparator_3 (.a(divider_1_rem), .b({8{1'b0}}), .gt(imp), .eq(comparator_3_eq));  // open: lt
  ROM rom_1 (.addr(counter_1_q), .data(rom_1_data));  // open: sel
  assign controlled_buffer_2_out = X ? rom_1_data : 8'bz;  // Controlled_Buffer controlled_buffer_2
  and and_1 (and_1_out, _3, imp);
  Multiplexer #(.width(8)) multiplexer_1 (
    .in0(controlled_buffer_2_out), .in1(res), .out(multiplexer_1_out), .sel(and_1_out));  // open: en
  Comparator comparator_4 (.a(rom_1_data), .b({8{1'b0}}), .eq(comparator_4_eq));  // open: gt, lt
  and and_2 (Y, _0_t, comparator_3_eq);
  Register register_1 (.D(multiplexer_1_out), .Q(register_1_q), .clk(clk), .clr(clr));  // open: en
  assign controlled_buffer_3_out = imp ? rom_1_data : 8'bz;  // Controlled_Buffer controlled_buffer_3
  Register register_2 (.D(controlled_buffer_3_out), .Q(register_2_q), .clk(clk), .clr(clr));  // open: en
  assign controlled_buffer_4_out = Y ? rom_1_data : 8'bz;  // Controlled_Buffer controlled_buffer_4
  and and_3 (and_3_out, comparator_4_eq, imp);
  Register register_3 (.D(controlled_buffer_4_out), .Q(register_3_q), .clk(clk), .clr(clr));  // open: en
  not not_1 (stop, and_3_out);
  Button button_1 (.out(clr));
  // Probe on retenu
  // Probe on res
  \unité_de_calcul_PARTIE_1  \unité_de_calcul_partie_1_1  (
    .in_1(register_1_q), .in_2(register_3_q), .in_3(register_2_q), .out_4(res),
    .out_5(\unité_de_calcul_partie_1_1_out_5 ));
  D_Flip_Flop d_ff_1 (.Q(retenu), .preset(\unité_de_calcul_partie_1_1_out_5 ), .reset(clr));  // open: clk, D, Qn, en

  // Notes on the sheet:
  //   contents of rom_1 (hex, n*v repeats v):
  //   5 3 c 1 11 4 2 2 16
endmodule

module \unité_de_calcul_PARTIE_3  (
);

  wire _0_t, _3, add, and_1_out, and_3_out, clk, clock_1_out, clr, comparator_1_eq, comparator_1_gt,
       comparator_3_eq, comparator_4_eq, imp, not_1_out, not_2_out, retenu, stop, subtractor_1_bout,
       \unité_de_calcul_partie_1_1_out_5 , X, Y;
  wire [7:0] addr, controlled_buffer_2_out, controlled_buffer_3_out, controlled_buffer_4_out,
       controlled_buffer_5_out, counter_1_q, divider_1_rem, multiplexer_1_out, multiplexer_2_out,
       register_1_q, register_2_q, register_3_q, res, rom_1_data;

  Clock clock_1 (.out(clock_1_out));
  or or_1 (_3, comparator_1_eq, comparator_1_gt);
  Counter counter_1 (.Q(counter_1_q), .clk(clk), .clr(clr));  // open: load, D, count, carry
  assign clk = stop ? clock_1_out : 1'bz;  // Controlled_Buffer controlled_buffer_1
  Comparator comparator_1 (.a(counter_1_q), .b(8'h3), .gt(comparator_1_gt), .eq(comparator_1_eq));  // open: lt
  Multiplexer #(.width(8)) multiplexer_1 (
    .in0(counter_1_q), .in1(addr), .out(multiplexer_1_out), .sel(add));  // open: en
  Comparator comparator_2 (.a(counter_1_q), .b({8{1'b0}}), .gt(_0_t), .eq(X));  // open: lt
  Divider divider_1 (.a(counter_1_q), .b(8'h2), .rem(divider_1_rem));  // open: out, upper
  Comparator comparator_3 (.a(divider_1_rem), .b({8{1'b0}}), .gt(imp), .eq(comparator_3_eq));  // open: lt
  ROM rom_1 (.addr(multiplexer_1_out), .data(rom_1_data));  // open: sel
  not not_1 (not_1_out, add);
  assign controlled_buffer_2_out = not_1_out ? rom_1_data : 8'bz;  // Controlled_Buffer controlled_buffer_2
  and and_1 (and_1_out, _3, imp);
  assign controlled_buffer_3_out = X ? rom_1_data : 8'bz;  // Controlled_Buffer controlled_buffer_3
  Multiplexer #(.width(8)) multiplexer_2 (
    .in0(controlled_buffer_3_out), .in1(res), .out(multiplexer_2_out), .sel(and_1_out));  // open: en
  Subtractor subtractor_1 (.a(controlled_buffer_2_out), .b(8'h80), .out(addr), .bout(subtractor_1_bout));  // open: bin
  and and_2 (Y, _0_t, comparator_3_eq);
  Register register_1 (.D(multiplexer_2_out), .Q(register_1_q), .clk(clk), .clr(clr));  // open: en
  assign controlled_buffer_4_out = imp ? rom_1_data : 8'bz;  // Controlled_Buffer controlled_buffer_4
  Comparator comparator_4 (.a(rom_1_data), .b({8{1'b0}}), .eq(comparator_4_eq));  // open: gt, lt
  not not_2 (not_2_out, subtractor_1_bout);
  Register register_2 (.D(controlled_buffer_4_out), .Q(register_2_q), .clk(clk), .clr(clr));  // open: en
  assign controlled_buffer_5_out = Y ? rom_1_data : 8'bz;  // Controlled_Buffer controlled_buffer_5
  and and_3 (and_3_out, comparator_4_eq, imp);
  D_Flip_Flop d_ff_1 (.Q(add), .preset(not_2_out), .reset(clk));  // open: clk, D, Qn, en
  Register register_3 (.D(controlled_buffer_5_out), .Q(register_3_q), .clk(clk), .clr(clr));  // open: en
  not not_3 (stop, and_3_out);
  Button button_1 (.out(clr));
  // Probe on retenu
  // Probe on res
  \unité_de_calcul_PARTIE_1  \unité_de_calcul_partie_1_1  (
    .in_1(register_1_q), .in_2(register_3_q), .in_3(register_2_q), .out_4(res),
    .out_5(\unité_de_calcul_partie_1_1_out_5 ));
  D_Flip_Flop d_ff_2 (.Q(retenu), .preset(\unité_de_calcul_partie_1_1_out_5 ));  // open: clk, D, Qn, en, reset

  // Notes on the sheet:
  //   contents of rom_1 (hex, n*v repeats v):
  //   8c 3 c 1 8d 4 2 2 16 0 0 0 5 11
endmodule
