// Logisim project Parie1.circ as structural Verilog: 3 circuits, main circuit unité de calcul
module \unité_de_calcul  (
  input  in_1,
  input  in_2,
  input  in_3,
  input  in_4,
  input  in_5,
  input  in_6,
  input  in_7,
  input  in_8,
  input  in_9,
  input  in_10,
  input  in_11,
  input  in_12,
  input  in_13,
  input  in_14,
  input  in_15,
  input  in_16,
  input  in_17,
  input  in_18,
  input  in_19,
  output [7:0] out_20,
  output out_21
);

  wire adder_1_cout, subtractor_1_bout;
  wire [7:0] adder_1_out, subtractor_1_out, \séquenseur_1_p6 , \séquenseur_1_p7 , \séquenseur_1_p11 ,
       \séquenseur_1_p12 ;

  Adder adder_1 (
    .a({in_8, in_7, in_6, in_5, in_4, in_3, in_2, in_1}),
    .b({in_16, in_15, in_14, in_13, in_12, in_11, in_10, in_9}), .out(adder_1_out), .cout(adder_1_cout));  // open: cin
  Subtractor subtractor_1 (
    .a({in_8, in_7, in_6, in_5, in_4, in_3, in_2, in_1}),
    .b({in_16, in_15, in_14, in_13, in_12, in_11, in_10, in_9}), .out(subtractor_1_out),
    .bout(subtractor_1_bout));  // open: bin
  // Séquenseur séquenseur_1: pin names not known; wires that end beside it: in_17, in_18, in_19, adder_1_out, subtractor_1_out, \séquenseur_1_p6 , \séquenseur_1_p7 , out_21, adder_1_cout, subtractor_1_bout, \séquenseur_1_p11 , \séquenseur_1_p12 , out_20
  Multiplier multiplier_1 (
    .a({in_8, in_7, in_6, in_5, in_4, in_3, in_2, in_1}),
    .b({in_16, in_15, in_14, in_13, in_12, in_11, in_10, in_9}), .out(\séquenseur_1_p6 ),
    .cout(\séquenseur_1_p11 ));  // open: cin
  Divider divider_1 (
    .a({in_8, in_7, in_6, in_5, in_4, in_3, in_2, in_1}),
    .b({in_16, in_15, in_14, in_13, in_12, in_11, in_10, in_9}), .out(\séquenseur_1_p7 ),
    .rem(\séquenseur_1_p12 ));  // open: upper
endmodule

module \Séquenseur  (
  input  [7:0] in_1,
  input  in_2,
  input  in_3,
  input  in_4,
  input  in_5,
  input  [7:0] in_6,
  input  [7:0] in_7,
  input  [7:0] in_8,
  input  in_9,
  input  in_10,
  input  in_11,
  output [7:0] out_12,
  output out_13
);

  wire and_1_out, and_2_out, and_3_out, and_4_p3, and_5_out, and_6_out, and_7_out, and_8_out, and_10_out,
       nor_1_out, nor_2_p3, nor_2_p4, nor_3_out, not_1_out, undriven;
  wire [7:0] \valideur_d_octét_1_out_3 , \valideur_d_octét_2_out_3 , \valideur_d_octét_3_out_3 ,
       \valideur_d_octét_4_out_3 ;

  and and_1 (and_1_out, in_9, in_10, undriven);
  nor nor_1 (nor_1_out, in_10, undriven, in_10, in_10, nor_2_p4);
  // NOR_Gate nor_2: pin names not known; wires that end beside it: in_10, in_11, nor_2_p3, nor_2_p4, in_9
  nor nor_3 (nor_3_out, nor_2_p3, in_9, in_11);
  not not_1 (not_1_out, in_11);
  and and_2 (and_2_out, in_9, nor_2_p4);
  and and_3 (and_3_out, in_10, nor_3_out);
  // AND_Gate and_4: pin names not known; wires that end beside it: and_1_out, not_1_out, and_4_p3
  \Valideur_d_octét  \valideur_d_octét_1  (.out_3(\valideur_d_octét_1_out_3 ), .in_2(and_2_out), .in_1(in_8));
  \Valideur_d_octét  \valideur_d_octét_2  (.out_3(\valideur_d_octét_2_out_3 ), .in_2(and_3_out), .in_1(in_7));
  \Valideur_d_octét  \valideur_d_octét_3  (.out_3(\valideur_d_octét_3_out_3 ), .in_2(and_4_p3), .in_1(in_6));
  and and_5 (and_5_out, nor_1_out, in_11);
  \Valideur_d_octét  \valideur_d_octét_4  (.out_3(\valideur_d_octét_4_out_3 ), .in_2(and_5_out), .in_1(in_1));
  assign out_12 = \valideur_d_octét_1_out_3  | \valideur_d_octét_2_out_3  | \valideur_d_octét_3_out_3  | \valideur_d_octét_4_out_3 ;  // OR_Gate or_1, 8 bits wide
  and and_6 (and_6_out, and_2_out, in_2);
  and and_7 (and_7_out, and_4_p3, in_4);
  and and_8 (and_8_out, and_3_out, in_3);
  and and_9 (out_13, and_6_out, and_8_out, and_7_out, and_10_out);
  and and_10 (and_10_out, and_5_out, in_5);
endmodule

module \Valideur_d_octét  (
  input  [7:0] in_1,
  input  in_2,
  output [7:0] out_3
);

  wire undriven, undriven_2, undriven_3, undriven_4, undriven_5, undriven_6, undriven_7;

  and and_1 (out_3[7], in_2, in_1[7], undriven);
  and and_2 (out_3[6], undriven, in_2, in_1[6], undriven_2);
  and and_3 (out_3[5], undriven_2, in_2, in_1[5], undriven_3);
  and and_4 (out_3[4], undriven_3, in_2, in_1[4], undriven_4);
  and and_5 (out_3[3], undriven_4, in_2, in_1[3], undriven_5);
  and and_6 (out_3[2], undriven_5, in_2, in_1[2], undriven_6);
  and and_7 (out_3[1], undriven_6, in_2, in_1[1], undriven_7);
  and and_8 (out_3[0], undriven_7, in_2, in_1[0]);
endmodule
